# Fritzing sketch basic_ir_receiver (saved by Fritzing 0.9.3b)
breadboards: 1

parts:
  Part1 = Arduino Uno (Rev3) - ICSP
  IR1 = TSOP312.., 314.. [package=THT]

nets:
  N1: Part1.A0, IR1.Data
  N2: Part1.5V, IR1.Vs
  GND: Part1.GND, IR1.GND
