# Fritzing sketch magi-spin (saved by Fritzing 0.9.3b)
breadboards: 1

parts:
  Part2 = Arduino Uno (Rev3) - ICSP
  IR2 = TSOP312.., 314.. [package=THT]
  J1 = Basic Servo

nets:
  N1: Part2.A0, IR2.Data
  N2: Part2.D9_PWM, J1.pulse
  GND: Part2.GND, IR2.GND, J1.gnd
  5V: Part2.5V, IR2.Vs, J1.vcc
